// Logisim project CSE332_Project.circ as structural Verilog
module main (
  output [11:0] out_1,
  output [11:0] out_2,
  output [2:0] out_3,
  output [8:0] out_4,
  output [2:0] RS,
  output [11:0] out_6,
  output [2:0] RT,
  output [11:0] out_8,
  output [11:0] out_9,
  output [2:0] out_10
);

  wire clock_1_out, control_unit_1_1_alu_src, control_unit_1_1_jump, control_unit_1_1_lw,
       control_unit_1_1_ram_register, control_unit_1_1_reg_dst, control_unit_1_1_sub, control_unit_1_1_sw,
       control_unit_1_1_write_enb;
  wire [1:0] control_unit_1_1_aluop;
  wire [2:0] multiplexer_2_out;
  wire [11:0] alu_file_1_result, bit_extender_1_out, bit_extender_2_out, multiplexer_1_out, ram_1_dout,
       register_1_q, register_file_1_out_8;

  Multiplexer #(.width(12)) multiplexer_1 (
    .in0({out_1[11:9], out_2[8:0]}), .in1(out_1), .out(multiplexer_1_out), .sel(control_unit_1_1_jump));
  assign bit_extender_1_out = {{11{1'b0}}, 1'b1};  // Bit_Extender bit_extender_1
  Register #(.width(12)) register_1 (.D(multiplexer_1_out), .Q(register_1_q), .clk(clock_1_out));  // open: en, clr
  Control_Unit_1 control_unit_1_1 (
    .Reg_Dst(control_unit_1_1_reg_dst), .Write_enb(control_unit_1_1_write_enb),
    .ALU_Src(control_unit_1_1_alu_src), .ALUOP(control_unit_1_1_aluop), .Sub(control_unit_1_1_sub),
    .Lw(control_unit_1_1_lw), .Sw(control_unit_1_1_sw), .Ram_register(control_unit_1_1_ram_register),
    .Jump(control_unit_1_1_jump), .Opcode(out_3));
  Adder #(.width(12)) adder_1 (
    .a(register_1_q), .b(bit_extender_1_out), .out({out_1[11:9], out_2[8:0]}));  // open: cin, cout
  ROM #(.addrWidth(12), .dataWidth(12)) rom_1 (.addr(register_1_q), .data({out_3, out_1[8:0]}));
  Clock clock_1 (.out(clock_1_out));
  Multiplexer #(.width(3)) multiplexer_2 (
    .in0(out_1[2:0]), .in1(out_1[5:3]), .out(multiplexer_2_out), .sel(control_unit_1_1_reg_dst));
  assign bit_extender_2_out = {{9{1'b0}}, out_1[2:0]};  // Bit_Extender bit_extender_2
  Register_file register_file_1 (
    .out_7(out_6), .out_8(register_file_1_out_8), .in_1(out_1[8:6]), .in_4(out_1[5:3]),
    .Write_Enable(control_unit_1_1_write_enb), .Write_Register(multiplexer_2_out), .in_5(out_9),
    .in_6(clock_1_out));
  Multiplexer #(.width(12)) multiplexer_3 (
    .in0(register_file_1_out_8), .in1(bit_extender_2_out), .out(out_8), .sel(control_unit_1_1_alu_src));
  ALU_file alu_file_1 (
    .Result(alu_file_1_result), .A(out_6), .B(out_8), .Bin(control_unit_1_1_sub),
    .ALUop(control_unit_1_1_aluop), .Cin(control_unit_1_1_sub));  // open: Zero, Overflow, Ain
  RAM #(.addrWidth(12), .dataWidth(12)) ram_1 (
    .addr(alu_file_1_result), .we(control_unit_1_1_sw), .oe(control_unit_1_1_lw), .clk(clock_1_out),
    .din(register_file_1_out_8), .dout(ram_1_dout));
  Multiplexer #(.width(12)) multiplexer_4 (
    .in0(alu_file_1_result), .in1(ram_1_dout), .out(out_9), .sel(control_unit_1_1_ram_register));

  assign out_2[11:9] = out_1[11:9];
  assign out_4 = out_1[8:0];
  assign out_10 = out_1[2:0];
  assign RS = out_1[8:6];
  assign RT = out_1[5:3];

  // Notes on the sheet:
  //   Next Instruction
  //   contents of rom_1 (hex, n*v repeats v):
  //   53 529 529 731 853 e00
  //   CLK
  //   Opcode
  //   RD/Imm
  //   Data 1
  //   Data 2
endmodule

module Register_file (
  input  [2:0] in_1,
  input  Write_Enable,
  input  [2:0] Write_Register,
  input  [2:0] in_4,
  input  [11:0] in_5,
  input  in_6,
  output [11:0] out_7,
  output [11:0] out_8
);

  wire demultiplexer_1_out0, demultiplexer_1_out1, demultiplexer_1_out2, demultiplexer_1_out3,
       demultiplexer_1_out4, demultiplexer_1_out5, demultiplexer_1_out6, demultiplexer_1_out7;
  wire [11:0] register_1_q, register_2_q, register_3_q, register_4_q, register_5_q, register_6_q,
       register_7_q, register_8_q;

  Demultiplexer #(.select(3)) demultiplexer_1 (
    .out0(demultiplexer_1_out0), .out1(demultiplexer_1_out1), .out2(demultiplexer_1_out2),
    .out3(demultiplexer_1_out3), .out4(demultiplexer_1_out4), .out5(demultiplexer_1_out5),
    .out6(demultiplexer_1_out6), .out7(demultiplexer_1_out7), .in(Write_Enable), .sel(Write_Register));
  Register #(.width(12)) register_1 (.D(in_5), .en(demultiplexer_1_out0), .Q(register_1_q), .clr(in_6));  // open: clk
  Register #(.width(12)) register_2 (.D(in_5), .en(demultiplexer_1_out1), .Q(register_2_q), .clk(in_6));  // open: clr
  Register #(.width(12)) register_3 (.D(in_5), .en(demultiplexer_1_out2), .Q(register_3_q), .clk(in_6));  // open: clr
  Register #(.width(12)) register_4 (.D(in_5), .en(demultiplexer_1_out3), .Q(register_4_q), .clk(in_6));  // open: clr
  Register #(.width(12)) register_5 (.D(in_5), .en(demultiplexer_1_out4), .Q(register_5_q), .clk(in_6));  // open: clr
  Register #(.width(12)) register_6 (.D(in_5), .en(demultiplexer_1_out5), .Q(register_6_q), .clk(in_6));  // open: clr
  Register #(.width(12)) register_7 (.D(in_5), .en(demultiplexer_1_out6), .Q(register_7_q), .clk(in_6));  // open: clr
  Register #(.width(12)) register_8 (.D(in_5), .en(demultiplexer_1_out7), .Q(register_8_q), .clk(in_6));  // open: clr
  Multiplexer #(.select(3), .width(12)) multiplexer_1 (
    .in0(register_1_q), .in1(register_2_q), .in2(register_3_q), .in3(register_4_q), .in4(register_5_q),
    .in5(register_6_q), .in6(register_7_q), .in7(register_8_q), .out(out_7), .sel(in_1));
  Multiplexer #(.select(3), .width(12)) multiplexer_2 (
    .in0(register_1_q), .in1(register_2_q), .in2(register_3_q), .in3(register_4_q), .in4(register_5_q),
    .in5(register_6_q), .in6(register_7_q), .in7(register_8_q), .out(out_8), .sel(in_4));

  // Notes on the sheet:
  //   16 bit Register file
  //   Write Data
  //   0
  //   1
  //   2
  //   3
  //   4
  //   5
  //   6
  //   7
  //   Clock
  //   Read Register - 1
  //   Read Register - 2
  //   Read Data - 1
  //   Read Data -2
endmodule

module ALU_file (
  input  Cin,
  input  [11:0] A,
  input  Ain,
  input  Bin,
  input  [1:0] ALUop,
  input  [11:0] B,
  output [11:0] Result,
  output Zero,
  output Overflow
);

  wire alu_1_bit_1_cout, alu_1_bit_2_cout, alu_1_bit_3_cout, alu_1_bit_4_cout, alu_1_bit_5_cout,
       alu_1_bit_6_cout, alu_1_bit_7_cout, alu_1_bit_8_cout, alu_1_bit_9_cout, alu_1_bit_10_cout,
       alu_1_bit_11_cout;

  ALU_1_Bit alu_1_bit_1 (
    .Cout(alu_1_bit_1_cout), .Output(Result[0]), .Ain(Ain), .Bin(Bin), .A(A[0]), .B(B[0]), .Cin(Cin),
    .ALUop(ALUop));
  ALU_1_Bit alu_1_bit_2 (
    .Cout(alu_1_bit_2_cout), .Output(Result[1]), .Ain(Ain), .Bin(Bin), .A(A[1]), .B(B[1]),
    .Cin(alu_1_bit_1_cout), .ALUop(ALUop));
  ALU_1_Bit alu_1_bit_3 (
    .Cout(alu_1_bit_3_cout), .Output(Result[2]), .Ain(Ain), .Bin(Bin), .A(A[2]), .B(B[2]),
    .Cin(alu_1_bit_2_cout), .ALUop(ALUop));
  ALU_1_Bit alu_1_bit_4 (
    .Cout(alu_1_bit_4_cout), .Output(Result[3]), .Ain(Ain), .Bin(Bin), .A(A[3]), .B(B[3]),
    .Cin(alu_1_bit_3_cout), .ALUop(ALUop));
  ALU_1_Bit alu_1_bit_5 (
    .Cout(alu_1_bit_5_cout), .Output(Result[4]), .Ain(Ain), .Bin(Bin), .A(A[4]), .B(B[4]),
    .Cin(alu_1_bit_4_cout), .ALUop(ALUop));
  ALU_1_Bit alu_1_bit_6 (
    .Cout(alu_1_bit_6_cout), .Output(Result[5]), .Ain(Ain), .Bin(Bin), .A(A[5]), .B(B[5]),
    .Cin(alu_1_bit_5_cout), .ALUop(ALUop));
  ALU_1_Bit alu_1_bit_7 (
    .Cout(alu_1_bit_7_cout), .Output(Result[6]), .Ain(Ain), .Bin(Bin), .A(A[6]), .B(B[6]),
    .Cin(alu_1_bit_6_cout), .ALUop(ALUop));
  ALU_1_Bit alu_1_bit_8 (
    .Cout(alu_1_bit_8_cout), .Output(Result[7]), .Ain(Ain), .Bin(Bin), .A(A[7]), .B(B[7]),
    .Cin(alu_1_bit_7_cout), .ALUop(ALUop));
  ALU_1_Bit alu_1_bit_9 (
    .Cout(alu_1_bit_9_cout), .Output(Result[8]), .Ain(Ain), .Bin(Bin), .A(A[8]), .B(B[8]),
    .Cin(alu_1_bit_8_cout), .ALUop(ALUop));
  ALU_1_Bit alu_1_bit_10 (
    .Cout(alu_1_bit_10_cout), .Output(Result[9]), .Ain(Ain), .Bin(Bin), .A(A[9]), .B(B[9]),
    .Cin(alu_1_bit_9_cout), .ALUop(ALUop));
  ALU_1_Bit alu_1_bit_11 (
    .Cout(alu_1_bit_11_cout), .Output(Result[10]), .Ain(Ain), .Bin(Bin), .A(A[10]), .B(B[10]),
    .Cin(alu_1_bit_10_cout), .ALUop(ALUop));
  ALU_1_Bit alu_1_bit_12 (
    .Output(Result[11]), .Ain(Ain), .Bin(Bin), .A(A[11]), .B(B[11]), .Cin(alu_1_bit_11_cout), .ALUop(ALUop));  // open: Cout
  nor nor_1 (Zero, Result[0], Result[1], Result[2], Result[3], Result[4], Result[5], Result[6], Result[7], Result[8], Result[9], Result[10], Result[11]);
  xor xor_1 (Overflow, alu_1_bit_11_cout, Result[11]);
endmodule

module ALU_1_Bit (
  input  Cin,
  input  A,
  input  Ain,
  input  B,
  input  [1:0] ALUop,
  input  Bin,
  output Output,
  output Cout
);

  wire adder_1_out, and_1_out, multiplexer_1_out, multiplexer_2_out, not_1_out, not_2_out, or_1_out,
       xor_1_out;

  not not_1 (not_1_out, A);
  not not_2 (not_2_out, B);
  Multiplexer multiplexer_1 (.in0(A), .in1(not_1_out), .out(multiplexer_1_out), .sel(Ain));
  Multiplexer multiplexer_2 (.in0(B), .in1(not_2_out), .out(multiplexer_2_out), .sel(Bin));
  and and_1 (and_1_out, multiplexer_1_out, multiplexer_2_out);
  or or_1 (or_1_out, multiplexer_1_out, multiplexer_2_out);
  xor xor_1 (xor_1_out, multiplexer_1_out, multiplexer_2_out);
  Adder #(.width(1)) adder_1 (.a(multiplexer_1_out), .b(multiplexer_2_out), .out(adder_1_out), .cin(Cin), .cout(Cout));
  Multiplexer #(.select(2)) multiplexer_3 (
    .in0(and_1_out), .in1(or_1_out), .in2(adder_1_out), .in3(xor_1_out), .out(Output), .sel(ALUop));
endmodule

module Control_Unit_1 (
  input  [2:0] Opcode,
  output Reg_Dst,
  output Write_enb,
  output ALU_Src,
  output [1:0] ALUOP,
  output Sub,
  output Lw,
  output Sw,
  output Ram_register,
  output Jump
);

  wire and_1_out, and_2_out, and_3_out, and_4_out, and_6_out, and_7_out, and_8_out, and_9_out, and_10_out,
       not_1_out, not_2_out, not_3_out, or_4_out;

  not not_1 (not_1_out, Opcode[2]);
  not not_2 (not_2_out, Opcode[1]);
  not not_3 (not_3_out, Opcode[0]);
  and and_1 (and_1_out, Opcode[1], not_3_out);
  and and_2 (and_2_out, Opcode[2], not_2_out);
  or or_1 (Write_enb, not_2_out, not_3_out);
  and and_3 (and_3_out, not_1_out, Opcode[1]);
  and and_4 (and_4_out, Opcode[2], not_2_out);
  or or_2 (ALUOP[1], not_1_out, not_2_out);
  and and_5 (Sub, not_2_out, Opcode[0]);
  and and_6 (and_6_out, not_1_out, Opcode[1]);
  and and_7 (and_7_out, not_1_out, Opcode[1]);
  and and_8 (and_8_out, not_1_out, Opcode[1]);
  and and_9 (and_9_out, Opcode[2], Opcode[1]);
  or or_3 (Reg_Dst, and_1_out, and_2_out);
  or or_4 (or_4_out, and_3_out, and_4_out);
  and and_10 (and_10_out, Opcode[2], not_3_out);
  and and_11 (Lw, and_6_out, not_3_out);
  and and_12 (Sw, and_7_out, Opcode[0]);
  and and_13 (Ram_register, and_8_out, not_3_out);
  and and_14 (Jump, and_9_out, Opcode[0]);
  or or_5 (ALU_Src, or_4_out, and_10_out);

  assign ALUOP[0] = 1'b0;
endmodule
