// Logisim project testFile1.circ as structural Verilog: 3 circuits, main circuit main
module main (
  input  in_1,
  input  in_2,
  input  in_3,
  input  in_4,
  input  in_5,
  input  in_6,
  input  in_7,
  input  in_8,
  output out_9,
  output out_10,
  output out_11,
  output out_12
);

  and and_1 (out_9, in_1, in_2);
  and and_2 (out_10, in_3, in_4);
  and and_3 (out_11, in_5, in_6);
  and and_4 (out_12, in_7, in_8);
endmodule

module L_1_bit_ALU_22ca6921 (
  input  Cin,
  input  A,
  input  Ain,
  input  B,
  input  [2:0] ALUop,
  input  Bin,
  output Output,
  output Cout
);

  wire adder_1_out, and_1_out, multiplexer_1_out, multiplexer_2_out, not_1_out, not_2_out, or_1_out,
       xor_1_out;

  not not_1 (not_1_out, A);
  not not_2 (not_2_out, B);
  Multiplexer multiplexer_1 (.in0(A), .in1(not_1_out), .out(multiplexer_1_out), .sel(Ain));
  Multiplexer multiplexer_2 (.in0(B), .in1(not_2_out), .out(multiplexer_2_out), .sel(Bin));
  and and_1 (and_1_out, multiplexer_1_out, multiplexer_2_out);
  or or_1 (or_1_out, multiplexer_1_out, multiplexer_2_out);
  xor xor_1 (xor_1_out, multiplexer_1_out, multiplexer_2_out);
  Adder #(.width(1)) adder_1 (.a(multiplexer_1_out), .b(multiplexer_2_out), .out(adder_1_out), .cin(Cin), .cout(Cout));
  Multiplexer #(.select(3)) multiplexer_3 (
    .in0(and_1_out), .in1(or_1_out), .in2(adder_1_out), .in3(xor_1_out), .out(Output), .sel(ALUop));  // open: in4, in5, in6, in7
endmodule

module L_12_bit_ALU_e981f24c (
  input  Cin,
  input  [11:0] A,
  input  Ain,
  input  Bin,
  input  [2:0] ALUop,
  input  [11:0] B,
  output [11:0] Result,
  output Zero,
  output Overflow
);

  wire l_1_bit_alu_22ca6921_1_cout, l_1_bit_alu_22ca6921_2_cout, l_1_bit_alu_22ca6921_3_cout,
       l_1_bit_alu_22ca6921_4_cout, l_1_bit_alu_22ca6921_5_cout, l_1_bit_alu_22ca6921_6_cout,
       l_1_bit_alu_22ca6921_7_cout, l_1_bit_alu_22ca6921_8_cout, l_1_bit_alu_22ca6921_9_cout,
       l_1_bit_alu_22ca6921_10_cout, l_1_bit_alu_22ca6921_11_cout;

  L_1_bit_ALU_22ca6921 l_1_bit_alu_22ca6921_1 (
    .Cout(l_1_bit_alu_22ca6921_1_cout), .Output(Result[0]), .Ain(Ain), .Bin(Bin), .A(A[0]), .B(A[5]),
    .Cin(Cin), .ALUop(ALUop));
  L_1_bit_ALU_22ca6921 l_1_bit_alu_22ca6921_2 (
    .Cout(l_1_bit_alu_22ca6921_2_cout), .Output(Result[1]), .Ain(Ain), .Bin(Bin), .A(A[1]), .B(B[1]),
    .Cin(l_1_bit_alu_22ca6921_1_cout), .ALUop(ALUop));
  L_1_bit_ALU_22ca6921 l_1_bit_alu_22ca6921_3 (
    .Cout(l_1_bit_alu_22ca6921_3_cout), .Output(Result[2]), .Ain(Ain), .Bin(Bin), .A(A[2]), .B(B[2]),
    .Cin(l_1_bit_alu_22ca6921_2_cout), .ALUop(ALUop));
  L_1_bit_ALU_22ca6921 l_1_bit_alu_22ca6921_4 (
    .Cout(l_1_bit_alu_22ca6921_4_cout), .Output(Result[3]), .Ain(Ain), .Bin(Bin), .A(A[3]), .B(A[5]),
    .Cin(l_1_bit_alu_22ca6921_3_cout), .ALUop(ALUop));
  L_1_bit_ALU_22ca6921 l_1_bit_alu_22ca6921_5 (
    .Cout(l_1_bit_alu_22ca6921_5_cout), .Output(Result[4]), .Ain(Ain), .Bin(Bin), .A(A[4]), .B(B[4]),
    .Cin(l_1_bit_alu_22ca6921_4_cout), .ALUop(ALUop));
  L_1_bit_ALU_22ca6921 l_1_bit_alu_22ca6921_6 (
    .Cout(l_1_bit_alu_22ca6921_6_cout), .Output(Result[5]), .Ain(Ain), .Bin(Bin), .A(A[5]), .B(B[5]),
    .Cin(l_1_bit_alu_22ca6921_5_cout), .ALUop(ALUop));
  L_1_bit_ALU_22ca6921 l_1_bit_alu_22ca6921_7 (
    .Cout(l_1_bit_alu_22ca6921_7_cout), .Output(Result[6]), .Ain(Ain), .Bin(Bin), .A(A[6]), .B(B[6]),
    .Cin(l_1_bit_alu_22ca6921_6_cout), .ALUop(ALUop));
  L_1_bit_ALU_22ca6921 l_1_bit_alu_22ca6921_8 (
    .Cout(l_1_bit_alu_22ca6921_8_cout), .Output(Result[7]), .Ain(Ain), .Bin(Bin), .A(A[7]), .B(B[7]),
    .Cin(l_1_bit_alu_22ca6921_7_cout), .ALUop(ALUop));
  L_1_bit_ALU_22ca6921 l_1_bit_alu_22ca6921_9 (
    .Cout(l_1_bit_alu_22ca6921_9_cout), .Output(Result[8]), .Ain(Ain), .Bin(Bin), .A(A[8]), .B(B[8]),
    .Cin(l_1_bit_alu_22ca6921_8_cout), .ALUop(ALUop));
  L_1_bit_ALU_22ca6921 l_1_bit_alu_22ca6921_10 (
    .Cout(l_1_bit_alu_22ca6921_10_cout), .Output(Result[9]), .Ain(Ain), .Bin(Bin), .A(A[9]), .B(B[9]),
    .Cin(l_1_bit_alu_22ca6921_9_cout), .ALUop(ALUop));
  L_1_bit_ALU_22ca6921 l_1_bit_alu_22ca6921_11 (
    .Cout(l_1_bit_alu_22ca6921_11_cout), .Output(Result[10]), .Ain(Ain), .Bin(Bin), .A(A[10]), .B(B[10]),
    .Cin(l_1_bit_alu_22ca6921_10_cout), .ALUop(ALUop));
  L_1_bit_ALU_22ca6921 l_1_bit_alu_22ca6921_12 (
    .Output(Result[11]), .Ain(Ain), .Bin(Bin), .A(A[11]), .B(B[11]), .Cin(l_1_bit_alu_22ca6921_11_cout),
    .ALUop(ALUop));  // open: Cout
  nor nor_1 (Zero, Result[0], Result[1], Result[2], Result[3], Result[4], Result[5], Result[6], Result[7], Result[8], Result[9], Result[10], Result[11]);
  xor xor_1 (Overflow, l_1_bit_alu_22ca6921_11_cout, Result[11]);

  assign {B[3], B[0]} = {2{A[5]}};
endmodule
